// Logisim project BIDIRECTIONAL_SHIFT_REGISTER.circ as structural Verilog: 1 circuit, main circuit main
module main (
  input  M,
  input  DR,
  input  DL
);

  wire and_1_out, and_2_out, and_3_out, and_4_out, and_5_out, and_6_out, and_7_out, and_8_out, clock_1_out,
       d_ff_1_q, d_ff_2_q, d_ff_3_q, d_ff_4_q, not_1_out, or_1_out, or_2_out, or_3_out, or_4_out;

  not not_1 (not_1_out, M);
  Clock clock_1 (.out(clock_1_out));
  and and_1 (and_1_out, DR, M);
  and and_2 (and_2_out, d_ff_2_q, not_1_out);
  or or_1 (or_1_out, and_1_out, and_2_out);
  and and_3 (and_3_out, d_ff_1_q, M);
  D_Flip_Flop #(.trigger("falling")) d_ff_1 (
    .clk(clock_1_out), .D(or_1_out), .Q(d_ff_1_q));  // open: Qn, preset, en, reset
  and and_4 (and_4_out, d_ff_3_q, not_1_out);
  or or_2 (or_2_out, and_3_out, and_4_out);
  LED led_1 (.in(d_ff_2_q));
  LED led_2 (.in(d_ff_1_q));
  LED led_3 (.in(d_ff_3_q));
  and and_5 (and_5_out, d_ff_2_q, M);
  D_Flip_Flop #(.trigger("falling")) d_ff_2 (
    .clk(clock_1_out), .D(or_2_out), .Q(d_ff_2_q));  // open: Qn, preset, en, reset
  LED led_4 (.in(d_ff_4_q));
  and and_6 (and_6_out, d_ff_4_q, not_1_out);
  or or_3 (or_3_out, and_5_out, and_6_out);
  D_Flip_Flop #(.trigger("falling")) d_ff_3 (
    .clk(clock_1_out), .D(or_3_out), .Q(d_ff_3_q));  // open: Qn, preset, en, reset
  and and_7 (and_7_out, d_ff_3_q, M);
  and and_8 (and_8_out, DL, not_1_out);
  or or_4 (or_4_out, and_7_out, and_8_out);
  D_Flip_Flop #(.trigger("falling")) d_ff_4 (
    .clk(clock_1_out), .D(or_4_out), .Q(d_ff_4_q));  // open: Qn, preset, en, reset

  // Notes on the sheet:
  //          M=1 RIGHT SHIFT REGISTER
  //    M=0 LEFT SHIFT REGISTER
  //   BIDIRECTIONAL SHIFT REGISTER
endmodule
