// Logisim project DECADE COUNTER.circ as structural Verilog: 2 circuits, main circuit main
module main (
  input  in_1,
  output out_2,
  output out_3,
  output _1,
  output out_5
);

  wire and_1_out, clock_1_out, j_k_ff_1_qn, j_k_ff_2_qn, j_k_ff_3_qn;

  Clock clock_1 (.out(clock_1_out));
  J_K_Flip_Flop j_k_ff_1 (
    .J(in_1), .clk(clock_1_out), .K(in_1), .Q(_1), .Qn(j_k_ff_1_qn), .en(in_1), .reset(and_1_out));  // open: preset
  LED led_1 (.in(_1));
  LED led_2 (.in(out_3));
  J_K_Flip_Flop j_k_ff_2 (
    .J(in_1), .clk(j_k_ff_1_qn), .K(in_1), .Q(out_3), .Qn(j_k_ff_2_qn), .en(in_1), .reset(and_1_out));  // open: preset
  LED led_3 (.in(out_2));
  LED led_4 (.in(out_5));
  J_K_Flip_Flop j_k_ff_3 (
    .J(in_1), .clk(j_k_ff_2_qn), .K(in_1), .Q(out_2), .Qn(j_k_ff_3_qn), .en(in_1), .reset(and_1_out));  // open: preset
  and and_1 (and_1_out, out_3, out_5);
  J_K_Flip_Flop j_k_ff_4 (
    .J(in_1), .clk(j_k_ff_3_qn), .K(in_1), .Q(out_5), .en(in_1), .reset(and_1_out));  // open: Qn, preset

  // Notes on the sheet:
  //   2
  //   1
  //   4
  //   8
  //   TRUNCATED MOD10 OR DECADE COUNTER
endmodule

module modd10 (
);

  main main_1 ();  // open: in_1, out_2, out_3, _1, out_5
endmodule
