// Logisim project TRAFFIC_LIGHT_PROJECT.circ as structural Verilog: 1 circuit, main circuit main
module main (
  input  X
);

  wire and_1_out, and_2_out, and_3_out, and_4_out, and_5_out, and_6_out, and_7_out, and_8_out, and_9_out,
       and_10_out, and_11_out, and_12_out, clock_1_out, j_k_ff_1_q, j_k_ff_1_qn, j_k_ff_2_q, j_k_ff_2_qn,
       j_k_ff_3_q, j_k_ff_3_qn, not_1_out, or_1_out, or_2_out, or_3_out, or_4_out, or_5_out, or_6_out,
       or_7_out, or_8_out;

  not not_1 (not_1_out, X);
  Clock clock_1 (.out(clock_1_out));
  and and_1 (and_1_out, j_k_ff_3_q, X);
  and and_2 (and_2_out, j_k_ff_1_qn, X);
  and and_3 (and_3_out, j_k_ff_2_qn, j_k_ff_1_qn, not_1_out);
  and and_4 (and_4_out, j_k_ff_2_q, j_k_ff_1_qn, X);
  and and_5 (and_5_out, j_k_ff_2_qn, j_k_ff_1_q, X);
  and and_6 (and_6_out, j_k_ff_2_q, j_k_ff_3_q, X);
  or or_1 (or_1_out, not_1_out, j_k_ff_2_q, j_k_ff_3_q);
  or or_2 (or_2_out, and_1_out, and_2_out);
  or or_3 (or_3_out, j_k_ff_3_q, not_1_out, j_k_ff_1_q);
  or or_4 (or_4_out, and_3_out, and_4_out, and_5_out);
  J_K_Flip_Flop #(.trigger("falling")) j_k_ff_1 (
    .J(and_6_out), .clk(clock_1_out), .K(or_1_out), .Q(j_k_ff_1_q), .Qn(j_k_ff_1_qn));  // open: preset, en, reset
  J_K_Flip_Flop #(.trigger("falling")) j_k_ff_2 (
    .J(or_2_out), .clk(clock_1_out), .K(or_3_out), .Q(j_k_ff_2_q), .Qn(j_k_ff_2_qn));  // open: preset, en, reset
  J_K_Flip_Flop #(.trigger("falling")) j_k_ff_3 (
    .J(or_4_out), .clk(clock_1_out), .K(j_k_ff_3_q), .Q(j_k_ff_3_q), .Qn(j_k_ff_3_qn));  // open: preset, en, reset
  and and_7 (and_7_out, j_k_ff_1_qn, j_k_ff_3_qn);
  and and_8 (and_8_out, j_k_ff_3_qn, j_k_ff_2_qn);
  or or_5 (or_5_out, and_7_out, j_k_ff_2_q);
  and and_9 (and_9_out, j_k_ff_3_q, j_k_ff_1_q, j_k_ff_2_qn);
  and and_10 (and_10_out, j_k_ff_1_q, j_k_ff_2_qn, j_k_ff_3_qn);
  or or_6 (or_6_out, and_8_out, j_k_ff_1_q);
  and and_11 (and_11_out, j_k_ff_1_qn, j_k_ff_2_q, j_k_ff_3_q);
  and and_12 (and_12_out, j_k_ff_1_qn, j_k_ff_2_q, j_k_ff_3_qn);
  or or_7 (or_7_out, or_5_out, and_9_out);
  LED led_1 (.in(or_5_out));
  LED led_2 (.in(and_9_out));
  LED led_3 (.in(and_10_out));
  or or_8 (or_8_out, or_6_out, and_11_out);
  LED led_4 (.in(or_7_out));
  LED led_5 (.in(and_10_out));
  LED led_6 (.in(or_6_out));
  LED led_7 (.in(and_11_out));
  LED led_8 (.in(and_12_out));
  LED led_9 (.in(or_8_out));
  LED led_10 (.in(and_12_out));

  // Notes on the sheet:
  //   R1
  //   Y1
  //   G1
  //   PEDESTRIAN CROSSING
  //   DW1
  //   W1
  //   TWO WAY TRAFFIC LIGHT
  //   R2
  //   Y2
  //   G2
  //   DW2
  //   W2
endmodule
